// Logisim project mips-like.circ as structural Verilog: 11 circuits, main circuit PROCESSADOR
module PROCESSADOR (
  output [31:0] \INSTRUÇÃO 
);

  wire and_1_out, button_1_out, clock_1_out, pipeline2_1_sbranch, pipeline2_1_sdatahazard,
       pipeline2_1_slermemoria, pipeline2_1_smultiplexadormemoria, pipeline2_1_sulamultiplexador,
       pipeline2_1_sulaop, pipeline2_1_swritememory, pipeline2_1_swriteregistrador, pipeline3_1_sbranch,
       \pipeline3_1_scomparação , pipeline3_1_slermemoria, pipeline3_1_smultiplexadormemoria,
       pipeline3_1_swritememory, pipeline3_1_swriteregistrador, pipeline4_1_smultiplexadormemoria,
       pipeline4_1_swriteregistrador, UC_branch, UC_datahazard, UC_escreverbr, UC_escrevermemoria,
       UC_lermemoria, UC_multiplexadormemoria, UC_multiplexadorula, UC_registradordestino, UC_ulaop,
       ula_1_bge;
  wire [3:0] multiplexer_1_out, pipeline2_1_sregistradordestino, pipeline3_1_sregistradordestino,
       pipeline4_1_sregistradordestino;
  wire [31:0] adder_1_out, adder_2_out, banco_de_registradores_1_r0_d, banco_de_registradores_1_r1_d,
       bit_extender_1_out, multiplexer_2_out, multiplexer_3_out, multiplexer_4_out, multiplexer_5_out, PC_q,
       pipeline1_1_spasso, pipeline2_1_simediato, pipeline2_1_sregistrador1, pipeline2_1_sregistrador2,
       pipeline3_1_sproximocomando, pipeline3_1_sula, pipeline3_1_swritememory_2, pipeline4_1_smemory,
       pipeline4_1_sula, ram_1_data, rom_1_data, shifter_1_out, ula_1_ula_out;

  Clock clock_1 (.out(clock_1_out));
  Register #(.width(32)) PC (.D(multiplexer_4_out), .Q(PC_q), .clk(clock_1_out), .clr(button_1_out));  // open: en
  Button button_1 (.out(button_1_out));
  Adder #(.width(32)) adder_1 (.a(32'h4), .b(PC_q), .out(adder_1_out));  // open: cin, cout
  ROM #(.dataWidth(32)) rom_1 (.addr(PC_q[9:2]), .data(rom_1_data));  // open: sel
  PipeLine1 pipeline1_1 (
    .EPasso(adder_1_out), .SPasso(pipeline1_1_spasso), .\EInstrução (rom_1_data), .\SInstrução (\INSTRUÇÃO ),
    .Clock(clock_1_out), .Clear(button_1_out));
  UC UC (
    .E3(\INSTRUÇÃO [31]), .E2(\INSTRUÇÃO [30]), .E1(\INSTRUÇÃO [29]), .E0(\INSTRUÇÃO [28]),
    .RegistradorDestino(UC_registradordestino), .Branch(UC_branch), .LerMemoria(UC_lermemoria),
    .MultiplexadorMemoria(UC_multiplexadormemoria), .ULAop(UC_ulaop), .EscreverMemoria(UC_escrevermemoria),
    .MultiplexadorULA(UC_multiplexadorula), .EscreverBR(UC_escreverbr), .DataHazard(UC_datahazard));  // open: Jump
  Multiplexer #(.width(4), .enable("false")) multiplexer_1 (
    .in0(\INSTRUÇÃO [23:20]), .in1(\INSTRUÇÃO [27:24]), .out(multiplexer_1_out), .sel(UC_registradordestino));
  BANCO_DE_REGISTRADORES banco_de_registradores_1 (
    .DATA_WRITE(multiplexer_5_out), .CLK(clock_1_out), .RWR(pipeline4_1_sregistradordestino),
    .R0_D(banco_de_registradores_1_r0_d), .R0(\INSTRUÇÃO [19:16]), .R1_D(banco_de_registradores_1_r1_d),
    .R1(\INSTRUÇÃO [23:20]), .RW(pipeline4_1_swriteregistrador), .RESET(button_1_out));
  assign bit_extender_1_out = {{16{\INSTRUÇÃO [15]}}, \INSTRUÇÃO [15:0]};  // Bit_Extender bit_extender_1
  PipeLine2 pipeline2_1 (
    .EBranch(UC_branch), .SBranch(pipeline2_1_sbranch), .Clock(clock_1_out), .Clear(button_1_out),
    .ELerMemoria(UC_lermemoria), .SLerMemoria(pipeline2_1_slermemoria),
    .EMultiplexadorMemoria(UC_multiplexadormemoria),
    .SMultiplexadorMemoria(pipeline2_1_smultiplexadormemoria), .EULAop(UC_ulaop),
    .SULAop(pipeline2_1_sulaop), .EWriteMemory(UC_escrevermemoria), .SWriteMemory(pipeline2_1_swritememory),
    .EULAMultiplexador(UC_multiplexadorula), .SULAMultiplexador(pipeline2_1_sulamultiplexador),
    .EWriteRegistrador(UC_escreverbr), .SWriteRegistrador(pipeline2_1_swriteregistrador),
    .EDataHazard(UC_datahazard), .SDataHazard(pipeline2_1_sdatahazard),
    .ERegistrador1(banco_de_registradores_1_r0_d), .SRegistrador1(pipeline2_1_sregistrador1),
    .ERegistrador2(banco_de_registradores_1_r1_d), .SRegistrador2(pipeline2_1_sregistrador2),
    .EImediato(bit_extender_1_out), .ERegistradorDestino(multiplexer_1_out),
    .SRegistradorDestino(pipeline2_1_sregistradordestino), .SImediato(pipeline2_1_simediato));
  Multiplexer #(.width(32), .enable("false")) multiplexer_2 (
    .in0(pipeline2_1_sregistrador1), .in1(pipeline3_1_sula), .out(multiplexer_2_out),
    .sel(pipeline2_1_sdatahazard));
  Shifter #(.width(32)) shifter_1 (.in(pipeline2_1_simediato), .\dist (5'b00010), .out(shifter_1_out));
  ULA ula_1 (
    .DATA_0(multiplexer_2_out), .DATA_1(multiplexer_3_out), .ULA_OUT(ula_1_ula_out),
    .ULA_OP(pipeline2_1_sulaop), .BGE(ula_1_bge));
  Multiplexer #(.width(32), .enable("false")) multiplexer_3 (
    .in0(pipeline2_1_sregistrador2), .in1(pipeline2_1_simediato), .out(multiplexer_3_out),
    .sel(pipeline2_1_sulamultiplexador));
  PipeLine3 pipeline3_1 (
    .EBranch(pipeline2_1_sbranch), .SBranch(pipeline3_1_sbranch), .ELerMemoria(pipeline2_1_slermemoria),
    .SLerMemoria(pipeline3_1_slermemoria), .EMultiplexadorMemoria(pipeline2_1_smultiplexadormemoria),
    .SMultiplexadorMemoria(pipeline3_1_smultiplexadormemoria), .EWriteMemory(pipeline2_1_swritememory),
    .SWriteMemory(pipeline3_1_swritememory), .EWriteRegistrador(pipeline2_1_swriteregistrador),
    .SWriteRegistrador(pipeline3_1_swriteregistrador), .EProximoComando(adder_2_out),
    .SProximoComando(pipeline3_1_sproximocomando), .\Ecomparação (ula_1_bge),
    .\Scomparação (\pipeline3_1_scomparação ), .EULA(ula_1_ula_out), .SULA(pipeline3_1_sula),
    .EWriteMemory_2(pipeline2_1_sregistrador2), .SWriteMemory_2(pipeline3_1_swritememory_2),
    .ERegistradorDestino(pipeline2_1_sregistradordestino),
    .SRegistradorDestino(pipeline3_1_sregistradordestino), .Clock(clock_1_out), .Clear(button_1_out));
  Adder #(.width(32)) adder_2 (.a(pipeline1_1_spasso), .b(shifter_1_out), .out(adder_2_out));  // open: cin, cout
  Multiplexer #(.width(32), .enable("false")) multiplexer_4 (
    .in0(adder_1_out), .in1(pipeline3_1_sproximocomando), .out(multiplexer_4_out), .sel(and_1_out));
  and and_1 (and_1_out, pipeline3_1_sbranch, \pipeline3_1_scomparação );
  RAM #(.addrWidth(24), .dataWidth(32), .bus("separate")) ram_1 (
    .addr(pipeline3_1_sula[23:0]), .din(pipeline3_1_swritememory_2), .data(ram_1_data),
    .str(pipeline3_1_swritememory), .clk(clock_1_out), .ld(pipeline3_1_slermemoria));  // open: sel, clr
  PipeLine4 pipeline4_1 (
    .EMultiplexadorMemoria(pipeline3_1_smultiplexadormemoria),
    .SMultiplexadorMemoria(pipeline4_1_smultiplexadormemoria),
    .EWriteRegistrador(pipeline3_1_swriteregistrador), .SWriteRegistrador(pipeline4_1_swriteregistrador),
    .EULA(pipeline3_1_sula), .SULA(pipeline4_1_sula), .EMemory(ram_1_data), .SMemory(pipeline4_1_smemory),
    .ERegistradorDestino(pipeline3_1_sregistradordestino),
    .SRegistradorDestino(pipeline4_1_sregistradordestino), .Clock(clock_1_out), .Clear(button_1_out));
  Multiplexer #(.width(32), .enable("false")) multiplexer_5 (
    .in0(pipeline4_1_sula), .in1(pipeline4_1_smemory), .out(multiplexer_5_out),
    .sel(pipeline4_1_smultiplexadormemoria));

  // Notes on the sheet:
  //   contents of rom_1 (hex, n*v repeats v):
  //   40ee0000 41ee0010 42ee0020 46ee0000 48ee0000 49ee0000 4bee0004 4fee0001 4*80000000 3eb60053
  //   4*80000000 47ee0000 4*80000000 3eb7003f 4*80000000 4aee0000 4*80000000 3eba0021 4*80000000 1c6b0000
  //   9cac0000 acfc0000 930c0000 4*80000000 53e30000 1cab0000 9c7c0000 acfc0000 941c0000 4*80000000
  //   54e40000 4*80000000 1c340000 999c0000 2aea0001 4*80000000 3eeeffdc 4*80000000 1c6b0000 9c7c0000
  //   acfc0000 952c0000 4*80000000 6e950000 49ee0000 27e70001 4*80000000 3eeeffbe 4*80000000 26e60001
  //   4*80000000 3eeeffaa 4*80000000
  //   REG_0
  //   REG_1
  //   REG_W
  //   DATA_W
  //   REG0_D
  //   REG1_D
  //   ULA
  //   Brach
endmodule

module ULA (
  input  [31:0] DATA_0,
  input  [31:0] DATA_1,
  input  ULA_OP,
  output BGE,
  output [31:0] ULA_OUT
);

  wire comparator_1_eq, comparator_1_gt;
  wire [31:0] adder_1_out, multiplier_1_out;

  Adder #(.width(32)) adder_1 (.a(DATA_0), .b(DATA_1), .out(adder_1_out));  // open: cin, cout
  Multiplier #(.width(32)) multiplier_1 (.a(DATA_0), .b(DATA_1), .out(multiplier_1_out));  // open: cin, cout
  Comparator #(.width(32), .mode("unsigned")) comparator_1 (
    .a(DATA_0), .b(DATA_1), .gt(comparator_1_gt), .eq(comparator_1_eq));  // open: lt
  Multiplexer #(.width(32), .enable("false")) multiplexer_1 (
    .in0(adder_1_out), .in1(multiplier_1_out), .out(ULA_OUT), .sel(ULA_OP));
  or or_1 (BGE, comparator_1_gt, comparator_1_eq);
endmodule

module UC (
  input  E3,
  input  E2,
  input  E1,
  input  E0,
  output RegistradorDestino,
  output Jump,
  output Branch,
  output LerMemoria,
  output MultiplexadorMemoria,
  output ULAop,
  output EscreverMemoria,
  output MultiplexadorULA,
  output EscreverBR,
  output DataHazard
);

  wire and_1_out, and_2_out, and_3_out, and_4_out, and_5_out, and_8_out, and_9_out, and_10_out, and_11_out,
       and_12_out, and_13_out, and_14_out, and_15_out, and_16_out, and_20_out, and_21_out, not_1_out,
       not_2_out, not_3_out, not_4_out, not_5_out, not_6_out, not_7_out, not_8_out, not_9_out, not_10_out,
       not_11_out, not_12_out, not_13_out, not_14_out, not_15_out, not_16_out, not_17_out, not_18_out,
       not_19_out, not_20_out, not_21_out, not_22_out, not_23_out, not_24_out, not_25_out, not_26_out,
       not_27_out, not_28_out, not_29_out, not_30_out;

  not not_1 (not_1_out, E3);
  and and_1 (and_1_out, not_1_out, not_2_out);
  not not_2 (not_2_out, E1);
  not not_3 (not_3_out, E1);
  and and_2 (and_2_out, not_3_out, E0);
  not not_4 (not_4_out, E2);
  and and_3 (and_3_out, not_4_out, E1, not_5_out);
  not not_5 (not_5_out, E0);
  and and_4 (and_4_out, E2, E0);
  and and_5 (and_5_out, E3, E2);
  and and_6 (Jump, E2, E1, E0);
  and and_7 (Branch, E1, E0);
  not not_6 (not_6_out, E3);
  not not_7 (not_7_out, E1);
  not not_8 (not_8_out, E3);
  not not_9 (not_9_out, E1);
  not not_10 (not_10_out, E3);
  and and_8 (and_8_out, not_10_out, not_11_out, E0);
  not not_11 (not_11_out, E2);
  not not_12 (not_12_out, E2);
  and and_9 (and_9_out, E3, not_12_out, E1);
  not not_13 (not_13_out, E3);
  not not_14 (not_14_out, E0);
  not not_15 (not_15_out, E3);
  and and_10 (and_10_out, not_15_out, E1, not_16_out);
  not not_16 (not_16_out, E0);
  not not_17 (not_17_out, E3);
  and and_11 (and_11_out, not_17_out, E2, not_18_out);
  not not_18 (not_18_out, E1);
  not not_19 (not_19_out, E1);
  and and_12 (and_12_out, E2, not_19_out, not_20_out);
  not not_20 (not_20_out, E0);
  not not_21 (not_21_out, E3);
  and and_13 (and_13_out, not_21_out, not_22_out);
  not not_22 (not_22_out, E1);
  not not_23 (not_23_out, E1);
  and and_14 (and_14_out, not_23_out, E0);
  not not_24 (not_24_out, E2);
  and and_15 (and_15_out, not_24_out, E1, not_25_out);
  not not_25 (not_25_out, E0);
  and and_16 (and_16_out, E2, not_26_out);
  not not_26 (not_26_out, E1);
  not not_27 (not_27_out, E2);
  not not_28 (not_28_out, E1);
  not not_29 (not_29_out, E2);
  not not_30 (not_30_out, E0);
  or or_1 (RegistradorDestino, and_1_out, and_2_out, and_3_out, and_4_out, and_5_out);
  and and_17 (LerMemoria, not_6_out, E2, not_7_out, E0);
  and and_18 (MultiplexadorMemoria, not_8_out, E2, not_9_out, E0);
  or or_2 (ULAop, and_8_out, and_9_out);
  and and_19 (EscreverMemoria, not_13_out, E2, E1, not_14_out);
  or or_3 (MultiplexadorULA, and_10_out, and_11_out, and_12_out);
  or or_4 (EscreverBR, and_13_out, and_14_out, and_15_out, and_16_out);
  and and_20 (and_20_out, E3, not_27_out, not_28_out, E0);
  or or_5 (DataHazard, and_20_out, and_21_out);
  and and_21 (and_21_out, E3, not_29_out, E1, not_30_out);
endmodule

module BANCO_DE_REGISTRADORES (
  input  [31:0] DATA_WRITE,
  input  [3:0] R0,
  input  [3:0] R1,
  input  CLK,
  input  [3:0] RWR,
  input  RESET,
  input  RW,
  output [31:0] R0_D,
  output [31:0] R1_D
);

  wire demultiplexer_1_out0, demultiplexer_1_out1, demultiplexer_1_out2, demultiplexer_1_out3,
       demultiplexer_1_out4, demultiplexer_1_out5, demultiplexer_1_out6, demultiplexer_1_out7,
       demultiplexer_1_out8, demultiplexer_1_out9, demultiplexer_1_out10, demultiplexer_1_out11,
       demultiplexer_1_out12, demultiplexer_1_out13, demultiplexer_1_out14, demultiplexer_1_out15;
  wire [31:0] register_1_q, register_2_q, register_3_q, register_4_q, register_5_q, register_6_q,
       register_7_q, register_8_q, register_9_q, register_10_q, register_11_q, register_12_q, register_13_q,
       register_14_q, register_15_q, register_16_q;

  Demultiplexer #(.select(4), .enable("false")) demultiplexer_1 (
    .out0(demultiplexer_1_out0), .out1(demultiplexer_1_out1), .out2(demultiplexer_1_out2),
    .out3(demultiplexer_1_out3), .out4(demultiplexer_1_out4), .out5(demultiplexer_1_out5),
    .out6(demultiplexer_1_out6), .out7(demultiplexer_1_out7), .out8(demultiplexer_1_out8),
    .out9(demultiplexer_1_out9), .out10(demultiplexer_1_out10), .out11(demultiplexer_1_out11),
    .out12(demultiplexer_1_out12), .out13(demultiplexer_1_out13), .out14(demultiplexer_1_out14),
    .out15(demultiplexer_1_out15), .in(RW), .sel(RWR));
  Register #(.width(32)) register_1 (
    .D(DATA_WRITE), .en(demultiplexer_1_out0), .Q(register_1_q), .clk(CLK), .clr(RESET));
  Register #(.width(32)) register_2 (
    .D(DATA_WRITE), .en(demultiplexer_1_out1), .Q(register_2_q), .clk(CLK), .clr(RESET));
  Register #(.width(32)) register_3 (
    .D(DATA_WRITE), .en(demultiplexer_1_out2), .Q(register_3_q), .clk(CLK), .clr(RESET));
  Register #(.width(32)) register_4 (
    .D(DATA_WRITE), .en(demultiplexer_1_out3), .Q(register_4_q), .clk(CLK), .clr(RESET));
  Register #(.width(32)) register_5 (
    .D(DATA_WRITE), .en(demultiplexer_1_out4), .Q(register_5_q), .clk(CLK), .clr(RESET));
  Register #(.width(32)) register_6 (
    .D(DATA_WRITE), .en(demultiplexer_1_out5), .Q(register_6_q), .clk(CLK), .clr(RESET));
  Register #(.width(32)) register_7 (
    .D(DATA_WRITE), .en(demultiplexer_1_out6), .Q(register_7_q), .clk(CLK), .clr(RESET));
  Register #(.width(32)) register_8 (
    .D(DATA_WRITE), .en(demultiplexer_1_out7), .Q(register_8_q), .clk(CLK), .clr(RESET));
  Register #(.width(32)) register_9 (
    .D(DATA_WRITE), .en(demultiplexer_1_out8), .Q(register_9_q), .clk(CLK), .clr(RESET));
  Register #(.width(32)) register_10 (
    .D(DATA_WRITE), .en(demultiplexer_1_out9), .Q(register_10_q), .clk(CLK), .clr(RESET));
  Register #(.width(32)) register_11 (
    .D(DATA_WRITE), .en(demultiplexer_1_out10), .Q(register_11_q), .clk(CLK), .clr(RESET));
  Register #(.width(32)) register_12 (
    .D(DATA_WRITE), .en(demultiplexer_1_out11), .Q(register_12_q), .clk(CLK), .clr(RESET));
  Register #(.width(32)) register_13 (
    .D(DATA_WRITE), .en(demultiplexer_1_out12), .Q(register_13_q), .clk(CLK), .clr(RESET));
  Register #(.width(32)) register_14 (
    .D(DATA_WRITE), .en(demultiplexer_1_out13), .Q(register_14_q), .clk(CLK), .clr(RESET));
  Register #(.width(32)) register_15 (
    .D(DATA_WRITE), .en(demultiplexer_1_out14), .Q(register_15_q), .clk(CLK), .clr(RESET));
  Register #(.width(32)) register_16 (
    .D(DATA_WRITE), .en(demultiplexer_1_out15), .Q(register_16_q), .clk(CLK), .clr(RESET));
  Multiplexer #(.select(4), .width(32), .disabled(0), .enable("false")) multiplexer_1 (
    .in0(register_1_q), .in1(register_2_q), .in2(register_3_q), .in3(register_4_q), .in4(register_5_q),
    .in5(register_6_q), .in6(register_7_q), .in7(register_8_q), .in8(register_9_q), .in9(register_10_q),
    .in10(register_11_q), .in11(register_12_q), .in12(register_13_q), .in13(register_14_q),
    .in14(register_15_q), .in15(register_16_q), .out(R0_D), .sel(R0));
  Multiplexer #(.select(4), .width(32), .enable("false")) multiplexer_2 (
    .in0(register_1_q), .in1(register_2_q), .in2(register_3_q), .in3(register_4_q), .in4(register_5_q),
    .in5(register_6_q), .in6(register_7_q), .in7(register_8_q), .in8(register_9_q), .in9(register_10_q),
    .in10(register_11_q), .in11(register_12_q), .in12(register_13_q), .in13(register_14_q),
    .in14(register_15_q), .in15(register_16_q), .out(R1_D), .sel(R1));

  // Notes on the sheet:
  //   T0
  //   T1
  //   T2
  //   T3
  //   T4
  //   T5
  //   T6
  //   T7
  //   S0
  //   S1
  //   S2
  //   S3
  //   S4
  //   S5
endmodule

module ShiftLeft2 (
  input  [31:0] E0,
  input  [31:0] E1,
  output [31:0] S1
);

  Shifter #(.width(28)) shifter_1 (.in({2'b00, E0[25:0]}), .\dist (5'b00010), .out(S1[27:0]));

  assign S1[31:28] = E1[31:28];
endmodule

module EstendeBits (
  input  [31:0] Epasso,
  input  [31:0] EInstrucao,
  output [31:0] SBranch
);

  wire [31:0] bit_extender_1_out, shifter_1_out;

  Adder #(.width(32)) adder_1 (.a(Epasso), .b(shifter_1_out), .out(SBranch));  // open: cin, cout
  Shifter #(.width(32)) shifter_1 (.in(bit_extender_1_out), .\dist (5'b00010), .out(shifter_1_out));
  assign bit_extender_1_out = {{16{EInstrucao[15]}}, EInstrucao[15:0]};  // Bit_Extender bit_extender_1
endmodule

module PipeLine1 (
  input  [31:0] EPasso,
  input  [31:0] \EInstrução ,
  input  Clock,
  input  Clear,
  output [31:0] SPasso,
  output [31:0] \SInstrução 
);

  Register #(.width(32)) register_1 (.D(EPasso), .Q(SPasso), .clk(Clock), .clr(Clear));  // open: en
  Register #(.width(32)) register_2 (.D(\EInstrução ), .Q(\SInstrução ), .clk(Clock), .clr(Clear));  // open: en
endmodule

module PipeLine2 (
  input  EBranch,
  input  ELerMemoria,
  input  EMultiplexadorMemoria,
  input  EULAop,
  input  EWriteMemory,
  input  EULAMultiplexador,
  input  EWriteRegistrador,
  input  EDataHazard,
  input  [31:0] ERegistrador1,
  input  [31:0] ERegistrador2,
  input  [31:0] EImediato,
  input  [3:0] ERegistradorDestino,
  input  Clock,
  input  Clear,
  output SBranch,
  output SLerMemoria,
  output SMultiplexadorMemoria,
  output SULAop,
  output SWriteMemory,
  output SULAMultiplexador,
  output SWriteRegistrador,
  output SDataHazard,
  output [31:0] SRegistrador1,
  output [31:0] SRegistrador2,
  output [31:0] SImediato,
  output [3:0] SRegistradorDestino
);

  Register #(.width(1)) register_1 (.D(EBranch), .Q(SBranch), .clk(Clock), .clr(Clear));  // open: en
  Register #(.width(1)) register_2 (.D(ELerMemoria), .Q(SLerMemoria), .clk(Clock), .clr(Clear));  // open: en
  Register #(.width(1)) register_3 (
    .D(EMultiplexadorMemoria), .Q(SMultiplexadorMemoria), .clk(Clock), .clr(Clear));  // open: en
  Register #(.width(1)) register_4 (.D(EULAop), .Q(SULAop), .clk(Clock), .clr(Clear));  // open: en
  Register #(.width(1)) register_5 (.D(EWriteMemory), .Q(SWriteMemory), .clk(Clock), .clr(Clear));  // open: en
  Register #(.width(1)) register_6 (
    .D(EULAMultiplexador), .Q(SULAMultiplexador), .clk(Clock), .clr(Clear));  // open: en
  Register #(.width(1)) register_7 (
    .D(EWriteRegistrador), .Q(SWriteRegistrador), .clk(Clock), .clr(Clear));  // open: en
  Register #(.width(1)) register_8 (.D(EDataHazard), .Q(SDataHazard), .clk(Clock), .clr(Clear));  // open: en
  Register #(.width(32)) register_9 (.D(ERegistrador1), .Q(SRegistrador1), .clk(Clock), .clr(Clear));  // open: en
  Register #(.width(32)) register_10 (.D(ERegistrador2), .Q(SRegistrador2), .clk(Clock), .clr(Clear));  // open: en
  Register #(.width(32)) register_11 (.D(EImediato), .Q(SImediato), .clk(Clock), .clr(Clear));  // open: en
  Register #(.width(4)) register_12 (
    .D(ERegistradorDestino), .Q(SRegistradorDestino), .clk(Clock), .clr(Clear));  // open: en
endmodule

module PipeLine3 (
  input  [31:0] EProximoComando,
  input  EMultiplexadorMemoria,
  input  EBranch,
  input  \Ecomparação ,
  input  EWriteMemory,
  input  ELerMemoria,
  input  EWriteRegistrador,
  input  [31:0] EULA,
  input  [31:0] EWriteMemory_2,
  input  [3:0] ERegistradorDestino,
  input  Clock,
  input  Clear,
  output [31:0] SProximoComando,
  output SMultiplexadorMemoria,
  output SBranch,
  output \Scomparação ,
  output SWriteMemory,
  output SLerMemoria,
  output SWriteRegistrador,
  output [31:0] SULA,
  output [31:0] SWriteMemory_2,
  output [3:0] SRegistradorDestino
);

  Register #(.width(32)) register_1 (.D(EProximoComando), .Q(SProximoComando), .clk(Clock), .clr(Clear));  // open: en
  Register #(.width(1)) register_2 (
    .D(EMultiplexadorMemoria), .Q(SMultiplexadorMemoria), .clk(Clock), .clr(Clear));  // open: en
  Register #(.width(1)) register_3 (.D(EBranch), .Q(SBranch), .clk(Clock), .clr(Clear));  // open: en
  Register #(.width(1)) register_4 (.D(\Ecomparação ), .Q(\Scomparação ), .clk(Clock), .clr(Clear));  // open: en
  Register #(.width(1)) register_5 (.D(EWriteMemory), .Q(SWriteMemory), .clk(Clock), .clr(Clear));  // open: en
  Register #(.width(1)) register_6 (.D(ELerMemoria), .Q(SLerMemoria), .clk(Clock), .clr(Clear));  // open: en
  Register #(.width(1)) register_7 (
    .D(EWriteRegistrador), .Q(SWriteRegistrador), .clk(Clock), .clr(Clear));  // open: en
  Register #(.width(32)) register_8 (.D(EULA), .Q(SULA), .clk(Clock), .clr(Clear));  // open: en
  Register #(.width(32)) register_9 (.D(EWriteMemory_2), .Q(SWriteMemory_2), .clk(Clock), .clr(Clear));  // open: en
  Register #(.width(4)) register_10 (
    .D(ERegistradorDestino), .Q(SRegistradorDestino), .clk(Clock), .clr(Clear));  // open: en
endmodule

module PipeLine4 (
  input  EMultiplexadorMemoria,
  input  EWriteRegistrador,
  input  [31:0] EULA,
  input  [31:0] EMemory,
  input  [3:0] ERegistradorDestino,
  input  Clock,
  input  Clear,
  output SMultiplexadorMemoria,
  output SWriteRegistrador,
  output [31:0] SULA,
  output [31:0] SMemory,
  output [3:0] SRegistradorDestino
);

  Register #(.width(1)) register_1 (
    .D(EMultiplexadorMemoria), .Q(SMultiplexadorMemoria), .clk(Clock), .clr(Clear));  // open: en
  Register #(.width(1)) register_2 (
    .D(EWriteRegistrador), .Q(SWriteRegistrador), .clk(Clock), .clr(Clear));  // open: en
  Register #(.width(32)) register_3 (.D(EULA), .Q(SULA), .clk(Clock), .clr(Clear));  // open: en
  Register #(.width(32)) register_4 (.D(EMemory), .Q(SMemory), .clk(Clock), .clr(Clear));  // open: en
  Register #(.width(4)) register_5 (
    .D(ERegistradorDestino), .Q(SRegistradorDestino), .clk(Clock), .clr(Clear));  // open: en
endmodule

module negador (
  input  [15:0] in_1,
  input  [15:0] in_2,
  output [15:0] out_3,
  output [15:0] out_4
);

  Negator #(.width(16)) negator_1 (.in(in_1), .out(out_3));
  Negator #(.width(16)) negator_2 (.in(in_2), .out(out_4));

  // Notes on the sheet:
  //   Volta
  //   Ida
endmodule
